# Fritzing sketch TempSensLEDSchematic (saved by Fritzing 0.9.2b)
circuit board: 8.46667cm x 5.64444cm
breadboards: 1

parts:
  Raspberry_Pi1 = Raspberry Pi B+
  R1 = Resistor [tolerance=±5% resistance=1k package="1206 [SMD]"]
  R2 = Resistor [tolerance=±5% resistance=1k package="1206 [SMD]"]
  C1 = Capacitor [package=cap-pth-small2]
  R3 = Temperature Sensor (Thermistor) [thermistor_type=NTC package=THT]
  LED1 = RGB LED (com. cathode, rgb) [package="5 mm [THT]"]
  R4 = Resistor [tolerance=±5% resistance=470 package="1206 [SMD]"]
  R5 = Resistor [tolerance=±5% resistance=470 package="1206 [SMD]"]
  R6 = Resistor [tolerance=±5% resistance=470 package="1206 [SMD]"]

nets (from the schematic view):
  N1: Raspberry_Pi1.GND, C1.2, LED1.common_cathode
  N2: Raspberry_Pi1.GPIO13, R5.Pin_1
  N3: Raspberry_Pi1.GPIO16, R6.Pin_1
  N4: Raspberry_Pi1.GPIO8, R4.Pin_1
  N5: Raspberry_Pi1.GPIO23, R2.Pin_1
  N6: Raspberry_Pi1.GPIO18, R1.Pin_1
  N7: R1.Pin_0, C1.1, R3.pin_0
  N8: R2.Pin_0, R3.pin_1
  N9: LED1.red_anode, R4.Pin_0
  N10: LED1.green_anode, R5.Pin_0
  N11: LED1.blue_anode, R6.Pin_0
